// Logisim project Obligatorio ARQ.circ as structural Verilog: 1 circuit, main circuit main
module main (
);

  wire and_1_out, and_2_out, and_3_out, and_4_out, button_4_out, button_5_out, button_6_out, button_7_out,
       clock_1_out, clock_2_out, counter_1_q;
  wire [2:0] RNG_out;
  wire [19:0] undriven, undriven_2, undriven_3, undriven_4;

  Button button_1 ();  // open: out
  Button button_2 ();  // open: out
  Button button_3 ();  // open: out
  LED led_1 ();  // open: in
  LED led_2 ();  // open: in
  LED led_3 ();  // open: in
  Clock clock_1 (.out(clock_1_out));
  Decoder #(.select(3)) decoder_1 (.sel(RNG_out));  // open: out0, out1, out2, out3, out4, out5, out6, out7, en
  Clock clock_2 (.out(clock_2_out));
  Random #(.width(3)) RNG (.clk(clock_1_out), .out(RNG_out));  // open: next, clr
  Shift_Register #(.length(5)) shift_register_1 (.clk(clock_2_out));  // open: shift, in, out, load, clr, d0, q0, d1, q1, d2, q2, d3, q3, d4, q4
  DotMatrix #(.matrixcols(9), .matrixrows(20)) dotmatrix_1 (
    .col1(undriven), .col3(undriven_2), .col5(undriven_3), .col6(undriven_3), .col7(undriven_4));  // open: col0, col2, col4, col8
  LED led_4 ();  // open: in
  Button button_4 (.out(button_4_out));
  LED led_5 ();  // open: in
  LED led_6 ();  // open: in
  LED led_7 ();  // open: in
  LED led_8 ();  // open: in
  Button button_5 (.out(button_5_out));
  Button button_6 (.out(button_6_out));
  Button button_7 (.out(button_7_out));
  LED led_9 ();  // open: in
  LED led_10 ();  // open: in
  LED led_11 ();  // open: in
  Counter #(.width(1), .max('h1)) counter_1 (.Q(counter_1_q));  // open: load, D, count, carry, clk, clr
  and and_1 (and_1_out, button_4_out, undriven[2]);
  and and_2 (and_2_out, button_7_out, undriven_2[2]);
  and and_3 (and_3_out, button_5_out, undriven_3[2]);
  and and_4 (and_4_out, button_6_out, undriven_4[2]);
  or or_1 (counter_1_q, and_1_out, and_2_out, and_3_out, and_4_out);

  // Notes on the sheet:
  //   Esperando juego
  //   Jugando
  //   Grabando
endmodule
