// Logisim project ObligatorioARQ.circ as structural Verilog: 5 circuits, main circuit main
module main (
  input  [11:0] in_1
);

  wire and_2_out, and_3_out, and_4_out, and_5_out, button_1_out, button_2_out, button_3_out, button_4_out,
       button_5_out, button_6_out, button_7_out, contadorpuntosbinario_1_led1, contadorpuntosbinario_1_led2,
       contadorpuntosbinario_1_led3, contadorpuntosbinario_1_led4, contadorpuntosbinario_1_led5,
       contadorpuntosbinario_1_led6, contadorpuntosbinario_1_led7, contadorpuntosbinario_1_led8,
       contadortiempo_1_reset, d_ff_1_q, decoder_1_out2, decoder_1_out3, decoder_1_out4, decoder_1_out5,
       grabacioncuadrados_1_pinluzgrabando, grabacioncuadrados_1_pinluzjugando,
       grabacioncuadrados_1_salidapuntaje, nor_1_out, or_1_out, or_2_out, or_3_out, RelojMatriz_out, RNG_p1;
  wire [2:0] undriven;
  wire [3:0] contadortiempo_1_mins, contadortiempo_1_segs, contadortiempo_1_segs2;
  wire [11:0] conectormatriz_1_out_10, conectormatriz_1_out_11, conectormatriz_1_out_12,
       conectormatriz_1_out_13, grabacioncuadrados_1_columna1, grabacioncuadrados_1_columna2,
       grabacioncuadrados_1_columna3, grabacioncuadrados_1_columna4, shift_register_1_out,
       shift_register_2_out, shift_register_3_out, shift_register_4_out;

  or or_1 (or_1_out, grabacioncuadrados_1_pinluzjugando, d_ff_1_q);
  nor nor_1 (nor_1_out, grabacioncuadrados_1_pinluzjugando, grabacioncuadrados_1_pinluzgrabando, d_ff_1_q);
  D_Flip_Flop d_ff_1 (.Q(d_ff_1_q), .preset(button_1_out), .reset(contadortiempo_1_reset));  // open: D, clk, Qn
  LED led_1 (.in(nor_1_out));
  LED led_2 (.in(or_1_out));
  LED led_3 (.in(grabacioncuadrados_1_pinluzgrabando));
  Clock RelojMatriz (.out(RelojMatriz_out));
  // Random #(.width(3)) RNG: pin names not known; wires that end beside it: RNG_p1
  and and_1 (RNG_p1, d_ff_1_q, RelojMatriz_out);
  Decoder #(.select(3)) decoder_1 (
    .out2(decoder_1_out2), .out3(decoder_1_out3), .out4(decoder_1_out4), .out5(decoder_1_out5), .sel(undriven));  // open: out0, out1, out6, out7, en
  Button button_1 (.out(button_1_out));
  Button button_2 (.out(button_2_out));
  Button button_3 (.out(button_3_out));
  grabacionCuadrados grabacioncuadrados_1 (
    .Boton1(button_4_out), .Boton2(button_5_out), .Boton3(button_6_out), .Boton4(button_7_out),
    .EntradaBotonGrabar(button_3_out), .EntradaJugarGrabacion(button_2_out),
    .salidaPuntaje(grabacioncuadrados_1_salidapuntaje), .Columna1(grabacioncuadrados_1_columna1),
    .PinLuzGrabando(grabacioncuadrados_1_pinluzgrabando), .Columna2(grabacioncuadrados_1_columna2),
    .Columna3(grabacioncuadrados_1_columna3), .Columna4(grabacioncuadrados_1_columna4),
    .PinLuzJugando(grabacioncuadrados_1_pinluzjugando));
  Shift_Register #(.length(12)) shift_register_1 (
    .in(decoder_1_out2), .clk(RNG_p1), .out(shift_register_1_out[0]), .clr(contadortiempo_1_reset),
    .q0(shift_register_1_out[11]), .q1(shift_register_1_out[10]), .q2(shift_register_1_out[9]),
    .q3(shift_register_1_out[8]), .q4(shift_register_1_out[7]), .q5(shift_register_1_out[6]),
    .q6(shift_register_1_out[5]), .q7(shift_register_1_out[4]), .q8(shift_register_1_out[3]),
    .q9(shift_register_1_out[2]), .q10(shift_register_1_out[1]));  // open: shift, load, d0, d1, d2, d3, d4, d5, d6, d7, d8, d9, d10, d11, q11
  Shift_Register #(.length(12)) shift_register_2 (
    .in(decoder_1_out3), .clk(RNG_p1), .out(shift_register_2_out[0]), .clr(contadortiempo_1_reset),
    .q0(shift_register_2_out[11]), .q1(shift_register_2_out[10]), .q2(shift_register_2_out[9]),
    .q3(shift_register_2_out[8]), .q4(shift_register_2_out[7]), .q5(shift_register_2_out[6]),
    .q6(shift_register_2_out[5]), .q7(shift_register_2_out[4]), .q8(shift_register_2_out[3]),
    .q9(shift_register_2_out[2]), .q10(shift_register_2_out[1]));  // open: shift, load, d0, d1, d2, d3, d4, d5, d6, d7, d8, d9, d10, d11, q11
  Shift_Register #(.length(12)) shift_register_3 (
    .in(decoder_1_out4), .clk(RNG_p1), .out(shift_register_3_out[0]), .clr(contadortiempo_1_reset),
    .q0(shift_register_3_out[11]), .q1(shift_register_3_out[10]), .q2(shift_register_3_out[9]),
    .q3(shift_register_3_out[8]), .q4(shift_register_3_out[7]), .q5(shift_register_3_out[6]),
    .q6(shift_register_3_out[5]), .q7(shift_register_3_out[4]), .q8(shift_register_3_out[3]),
    .q9(shift_register_3_out[2]), .q10(shift_register_3_out[1]));  // open: shift, load, d0, d1, d2, d3, d4, d5, d6, d7, d8, d9, d10, d11, q11
  Shift_Register #(.length(12)) shift_register_4 (
    .in(decoder_1_out5), .clk(RNG_p1), .out(shift_register_4_out[0]), .clr(contadortiempo_1_reset),
    .q0(shift_register_4_out[11]), .q1(shift_register_4_out[10]), .q2(shift_register_4_out[9]),
    .q3(shift_register_4_out[8]), .q4(shift_register_4_out[7]), .q5(shift_register_4_out[6]),
    .q6(shift_register_4_out[5]), .q7(shift_register_4_out[4]), .q8(shift_register_4_out[3]),
    .q9(shift_register_4_out[2]), .q10(shift_register_4_out[1]));  // open: shift, load, d0, d1, d2, d3, d4, d5, d6, d7, d8, d9, d10, d11, q11
  DotMatrix #(.matrixcols(9), .matrixrows(12)) dotmatrix_1 (
    .col0(in_1), .col1(conectormatriz_1_out_12), .col2(in_1), .col3(conectormatriz_1_out_13), .col4(in_1),
    .col5(conectormatriz_1_out_10), .col6(in_1), .col7(conectormatriz_1_out_11), .col8(in_1));
  ConectorMatriz conectormatriz_1 (
    .PINConfig(d_ff_1_q), .COL3GRABAR(grabacioncuadrados_1_columna3),
    .COL4GRABAR(grabacioncuadrados_1_columna4), .COL1GRABAR(grabacioncuadrados_1_columna1),
    .COL2GRABAR(grabacioncuadrados_1_columna2), .out_12(conectormatriz_1_out_12),
    .out_13(conectormatriz_1_out_13), .out_10(conectormatriz_1_out_10), .out_11(conectormatriz_1_out_11),
    .in_8(shift_register_1_out), .in_9(shift_register_2_out), .in_6(shift_register_3_out),
    .in_7(shift_register_4_out));
  Hex_Digit_Display hex_digit_display_1 (.value(contadortiempo_1_mins));  // open: dp
  Button button_4 (.out(button_4_out));
  and and_2 (and_2_out, button_4_out, shift_register_1_out[2]);
  and and_3 (and_3_out, button_5_out, shift_register_2_out[2]);
  and and_4 (and_4_out, button_6_out, shift_register_3_out[2]);
  and and_5 (and_5_out, button_7_out, shift_register_4_out[2]);
  Hex_Digit_Display hex_digit_display_2 (.value(contadortiempo_1_segs2));  // open: dp
  Button button_5 (.out(button_5_out));
  Button button_6 (.out(button_6_out));
  Button button_7 (.out(button_7_out));
  Hex_Digit_Display hex_digit_display_3 (.value(contadortiempo_1_segs));  // open: dp
  ContadorPuntosBinario contadorpuntosbinario_1 (
    .ENTRADA(or_2_out), .RESET(or_3_out), .Led1(contadorpuntosbinario_1_led1),
    .Led2(contadorpuntosbinario_1_led2), .Led3(contadorpuntosbinario_1_led3),
    .Led4(contadorpuntosbinario_1_led4), .Led5(contadorpuntosbinario_1_led5),
    .Led6(contadorpuntosbinario_1_led6), .Led7(contadorpuntosbinario_1_led7),
    .Led8(contadorpuntosbinario_1_led8));
  LED led_4 (.in(contadorpuntosbinario_1_led8));
  LED led_5 (.in(contadorpuntosbinario_1_led7));
  LED led_6 (.in(contadorpuntosbinario_1_led6));
  LED led_7 (.in(contadorpuntosbinario_1_led5));
  or or_2 (or_2_out, and_2_out, and_3_out, grabacioncuadrados_1_salidapuntaje, and_4_out, and_5_out);
  or or_3 (or_3_out, button_1_out, button_2_out);
  LED led_8 (.in(contadorpuntosbinario_1_led4));
  LED led_9 (.in(contadorpuntosbinario_1_led3));
  LED led_10 (.in(contadorpuntosbinario_1_led2));
  LED led_11 (.in(contadorpuntosbinario_1_led1));
  ContadorTiempo contadortiempo_1 (
    .in_1(RNG_p1), .Mins(contadortiempo_1_mins), .Segs2(contadortiempo_1_segs2),
    .Segs(contadortiempo_1_segs), .Reset(contadortiempo_1_reset));

  // Notes on the sheet:
  //   Esperando modo
  //   Jugando
  //   Grabando
  //   Grabar
  //   Jugar random
  //   Jugar grabacion
  //   ORTquestra
  //   ____
  //   :
  //   Contador puntos en binario:
endmodule

module ContadorTiempo (
  input  in_1,
  output [3:0] Mins,
  output [3:0] Segs2,
  output [3:0] Segs,
  output Reset
);

  wire and_1_out, clock_1_out, counter_2_carry, counter_3_carry, d_ff_1_q;

  Clock clock_1 (.out(clock_1_out));
  D_Flip_Flop d_ff_1 (.Q(d_ff_1_q), .preset(in_1), .reset(Reset));  // open: D, clk, Qn
  and and_1 (and_1_out, d_ff_1_q, clock_1_out);
  Counter #(.max('h2), .trigger("falling"), .width(4)) counter_1 (
    .clr(Reset), .clk(counter_2_carry), .carry(Reset), .Q(Mins));  // open: load, up, count, D
  Counter #(.max('h5), .trigger("falling"), .width(4)) counter_2 (
    .clr(Reset), .clk(counter_3_carry), .carry(counter_2_carry), .Q(Segs2));  // open: load, up, count, D
  Counter #(.max('h9), .width(4)) counter_3 (
    .clr(Reset), .clk(and_1_out), .carry(counter_3_carry), .Q(Segs));  // open: load, up, count, D
endmodule

module ContadorPuntosBinario (
  input  ENTRADA,
  input  RESET,
  output Led1,
  output Led2,
  output Led3,
  output Led4,
  output Led5,
  output Led6,
  output Led7,
  output Led8
);

  wire and_1_out, and_2_out, and_3_out, and_4_out, and_5_out, and_6_out;

  J_K_Flip_Flop j_k_ff_1 (.J(ENTRADA), .K(ENTRADA), .clk(ENTRADA), .Q(Led1), .reset(RESET));  // open: Qn, preset
  and and_1 (and_1_out, Led1, Led2);
  J_K_Flip_Flop j_k_ff_2 (.J(Led1), .K(Led1), .clk(ENTRADA), .Q(Led2), .reset(RESET));  // open: Qn, preset
  and and_2 (and_2_out, and_1_out, Led3);
  J_K_Flip_Flop j_k_ff_3 (.J(and_1_out), .K(and_1_out), .clk(ENTRADA), .Q(Led3), .reset(RESET));  // open: Qn, preset
  J_K_Flip_Flop j_k_ff_4 (.J(and_2_out), .K(and_2_out), .clk(ENTRADA), .Q(Led4), .reset(RESET));  // open: Qn, preset
  and and_3 (and_3_out, and_2_out, Led4);
  J_K_Flip_Flop j_k_ff_5 (.J(and_3_out), .K(and_3_out), .clk(ENTRADA), .Q(Led5), .reset(RESET));  // open: Qn, preset
  and and_4 (and_4_out, and_3_out, Led5);
  and and_5 (and_5_out, and_4_out, Led6);
  J_K_Flip_Flop j_k_ff_6 (.J(and_4_out), .K(and_4_out), .clk(ENTRADA), .Q(Led6), .reset(RESET));  // open: Qn, preset
  and and_6 (and_6_out, and_5_out, Led7);
  J_K_Flip_Flop j_k_ff_7 (.J(and_5_out), .K(and_5_out), .clk(ENTRADA), .Q(Led7), .reset(RESET));  // open: Qn, preset
  J_K_Flip_Flop j_k_ff_8 (.J(and_6_out), .K(and_6_out), .clk(ENTRADA), .Q(Led8), .reset(RESET));  // open: Qn, preset
endmodule

module grabacionCuadrados (
  input  Boton1,
  input  Boton2,
  input  Boton3,
  input  Boton4,
  input  EntradaBotonGrabar,
  input  EntradaJugarGrabacion,
  output salidaPuntaje,
  output [11:0] Columna1,
  output PinLuzGrabando,
  output [11:0] Columna2,
  output [11:0] Columna3,
  output [11:0] Columna4,
  output PinLuzJugando
);

  wire and_2_out, and_3_out, and_4_out, and_5_out, and_6_out, and_7_out, clock_1_out, clock_2_out,
       counter_1_carry, decoder_1_out2, decoder_1_out3, decoder_1_out4, decoder_1_out5, decoder_2_out1,
       decoder_2_out2, decoder_2_out4, decoder_2_out8, not_1_out, not_2_out, or_1_out, random_1_p1;
  wire [2:0] undriven;
  wire [3:0] ram_1_dout, shift_register_5_q0;
  wire [4:0] counter_1_q;
  wire [11:0] shift_register_1_out, shift_register_2_out, shift_register_3_out, shift_register_4_out,
       shift_register_6_q11, shift_register_7_q11, shift_register_8_q11, shift_register_9_q11;

  // Random #(.width(3)) random_1: pin names not known; wires that end beside it: random_1_p1
  and and_1 (random_1_p1, and_2_out, PinLuzGrabando);
  J_K_Flip_Flop j_k_ff_1 (
    .J(EntradaBotonGrabar), .K(EntradaBotonGrabar), .clk(EntradaBotonGrabar), .Q(PinLuzGrabando),
    .reset(counter_1_carry));  // open: Qn, preset
  Decoder #(.select(3)) decoder_1 (
    .out2(decoder_1_out2), .out3(decoder_1_out3), .out4(decoder_1_out4), .out5(decoder_1_out5), .sel(undriven));  // open: out0, out1, out6, out7, en
  Shift_Register #(.length(12)) shift_register_1 (
    .in(decoder_1_out2), .clk(and_2_out), .out(shift_register_1_out[0]), .load(not_1_out), .clr(not_1_out),
    .q0(shift_register_1_out[11]), .q1(shift_register_1_out[10]), .q2(shift_register_1_out[9]),
    .q3(shift_register_1_out[8]), .q4(shift_register_1_out[7]), .q5(shift_register_1_out[6]),
    .q6(shift_register_1_out[5]), .q7(shift_register_1_out[4]), .q8(shift_register_1_out[3]),
    .q9(shift_register_1_out[2]), .q10(shift_register_1_out[1]));  // open: shift, d0, d1, d2, d3, d4, d5, d6, d7, d8, d9, d10, d11, q11
  Shift_Register #(.length(12)) shift_register_2 (
    .in(decoder_1_out3), .clk(and_2_out), .out(shift_register_2_out[0]), .load(not_1_out), .clr(not_1_out),
    .q0(shift_register_2_out[11]), .q1(shift_register_2_out[10]), .q2(shift_register_2_out[9]),
    .q3(shift_register_2_out[8]), .q4(shift_register_2_out[7]), .q5(shift_register_2_out[6]),
    .q6(shift_register_2_out[5]), .q7(shift_register_2_out[4]), .q8(shift_register_2_out[3]),
    .q9(shift_register_2_out[2]), .q10(shift_register_2_out[1]));  // open: shift, d0, d1, d2, d3, d4, d5, d6, d7, d8, d9, d10, d11, q11
  Shift_Register #(.length(12)) shift_register_3 (
    .in(decoder_1_out4), .clk(and_2_out), .out(shift_register_3_out[0]), .load(not_1_out), .clr(not_1_out),
    .q0(shift_register_3_out[11]), .q1(shift_register_3_out[10]), .q2(shift_register_3_out[9]),
    .q3(shift_register_3_out[8]), .q4(shift_register_3_out[7]), .q5(shift_register_3_out[6]),
    .q6(shift_register_3_out[5]), .q7(shift_register_3_out[4]), .q8(shift_register_3_out[3]),
    .q9(shift_register_3_out[2]), .q10(shift_register_3_out[1]));  // open: shift, d0, d1, d2, d3, d4, d5, d6, d7, d8, d9, d10, d11, q11
  not not_1 (not_1_out, PinLuzGrabando);
  Shift_Register #(.length(12)) shift_register_4 (
    .in(decoder_1_out5), .clk(and_2_out), .out(shift_register_4_out[0]), .load(not_1_out), .clr(not_1_out),
    .q0(shift_register_4_out[11]), .q1(shift_register_4_out[10]), .q2(shift_register_4_out[9]),
    .q3(shift_register_4_out[8]), .q4(shift_register_4_out[7]), .q5(shift_register_4_out[6]),
    .q6(shift_register_4_out[5]), .q7(shift_register_4_out[4]), .q8(shift_register_4_out[3]),
    .q9(shift_register_4_out[2]), .q10(shift_register_4_out[1]));  // open: shift, d0, d1, d2, d3, d4, d5, d6, d7, d8, d9, d10, d11, q11
  and and_2 (and_2_out, PinLuzGrabando, clock_1_out);
  Clock clock_1 (.out(clock_1_out));
  Clock clock_2 (.out(clock_2_out));
  Counter #(.max('h1f), .width(5)) counter_1 (
    .Q(counter_1_q), .carry(counter_1_carry), .clk(or_1_out), .clr(counter_1_carry));  // open: load, D, count, up
  or or_1 (or_1_out, and_2_out, and_3_out);
  and and_3 (and_3_out, clock_2_out, PinLuzJugando);
  RAM #(.addrWidth(5), .dataWidth(4)) ram_1 (
    .addr(counter_1_q), .we(PinLuzGrabando), .oe(PinLuzJugando), .clk(or_1_out),
    .din({shift_register_4_out[11], shift_register_3_out[11], shift_register_2_out[11], shift_register_1_out[11]}),
    .dout(ram_1_dout));
  J_K_Flip_Flop j_k_ff_2 (
    .J(EntradaJugarGrabacion), .K(EntradaJugarGrabacion), .clk(EntradaJugarGrabacion), .Q(PinLuzJugando),
    .reset(counter_1_carry));  // open: Qn, preset
  Shift_Register #(.length(12), .width(4)) shift_register_5 (
    .in(ram_1_dout), .clk(and_3_out), .clr(EntradaJugarGrabacion), .q0(shift_register_5_q0));  // open: shift, out, load, d0, d1, q1, d2, q2, d3, q3, d4, q4, d5, q5, d6, q6, d7, q7, d8, q8, d9, q9, d10, q10, d11, q11
  Decoder #(.select(4)) decoder_2 (
    .out1(decoder_2_out1), .out2(decoder_2_out2), .out4(decoder_2_out4), .out8(decoder_2_out8),
    .sel(shift_register_5_q0));  // open: out0, out3, out5, out6, out7, out9, out10, out11, out12, out13, out14, out15, en
  Shift_Register #(.length(12)) shift_register_6 (
    .in(decoder_2_out1), .clk(and_3_out), .clr(EntradaJugarGrabacion), .q0(shift_register_6_q11[11]),
    .q1(shift_register_6_q11[10]), .q2(shift_register_6_q11[9]), .q3(shift_register_6_q11[8]),
    .q4(shift_register_6_q11[7]), .q5(shift_register_6_q11[6]), .q6(shift_register_6_q11[5]),
    .q7(shift_register_6_q11[4]), .q8(shift_register_6_q11[3]), .q9(shift_register_6_q11[2]),
    .q10(shift_register_6_q11[1]), .q11(shift_register_6_q11[0]));  // open: shift, out, load, d0, d1, d2, d3, d4, d5, d6, d7, d8, d9, d10, d11
  Shift_Register #(.length(12)) shift_register_7 (
    .in(decoder_2_out2), .clk(and_3_out), .clr(EntradaJugarGrabacion), .q0(shift_register_7_q11[11]),
    .q1(shift_register_7_q11[10]), .q2(shift_register_7_q11[9]), .q3(shift_register_7_q11[8]),
    .q4(shift_register_7_q11[7]), .q5(shift_register_7_q11[6]), .q6(shift_register_7_q11[5]),
    .q7(shift_register_7_q11[4]), .q8(shift_register_7_q11[3]), .q9(shift_register_7_q11[2]),
    .q10(shift_register_7_q11[1]), .q11(shift_register_7_q11[0]));  // open: shift, out, load, d0, d1, d2, d3, d4, d5, d6, d7, d8, d9, d10, d11
  Shift_Register #(.length(12)) shift_register_8 (
    .in(decoder_2_out4), .clk(and_3_out), .clr(EntradaJugarGrabacion), .q0(shift_register_8_q11[11]),
    .q1(shift_register_8_q11[10]), .q2(shift_register_8_q11[9]), .q3(shift_register_8_q11[8]),
    .q4(shift_register_8_q11[7]), .q5(shift_register_8_q11[6]), .q6(shift_register_8_q11[5]),
    .q7(shift_register_8_q11[4]), .q8(shift_register_8_q11[3]), .q9(shift_register_8_q11[2]),
    .q10(shift_register_8_q11[1]), .q11(shift_register_8_q11[0]));  // open: shift, out, load, d0, d1, d2, d3, d4, d5, d6, d7, d8, d9, d10, d11
  Shift_Register #(.length(12)) shift_register_9 (
    .in(decoder_2_out8), .clk(and_3_out), .clr(EntradaJugarGrabacion), .q0(shift_register_9_q11[11]),
    .q1(shift_register_9_q11[10]), .q2(shift_register_9_q11[9]), .q3(shift_register_9_q11[8]),
    .q4(shift_register_9_q11[7]), .q5(shift_register_9_q11[6]), .q6(shift_register_9_q11[5]),
    .q7(shift_register_9_q11[4]), .q8(shift_register_9_q11[3]), .q9(shift_register_9_q11[2]),
    .q10(shift_register_9_q11[1]), .q11(shift_register_9_q11[0]));  // open: shift, out, load, d0, d1, d2, d3, d4, d5, d6, d7, d8, d9, d10, d11
  not not_2 (not_2_out, PinLuzJugando);
  Multiplexer #(.width(12)) multiplexer_1 (
    .in0(shift_register_6_q11), .in1(shift_register_1_out), .out(Columna1), .sel(not_2_out));
  Multiplexer #(.width(12)) multiplexer_2 (
    .in0(shift_register_8_q11), .in1(shift_register_2_out), .out(Columna2), .sel(not_2_out));
  Multiplexer #(.width(12)) multiplexer_3 (
    .in0(shift_register_7_q11), .in1(shift_register_3_out), .out(Columna3), .sel(not_2_out));
  Multiplexer #(.width(12)) multiplexer_4 (
    .in0(shift_register_9_q11), .in1(shift_register_4_out), .out(Columna4), .sel(not_2_out));
  and and_4 (and_4_out, Boton1, shift_register_6_q11[2]);
  and and_5 (and_5_out, Boton2, shift_register_8_q11[2]);
  and and_6 (and_6_out, Boton3, shift_register_7_q11[3]);
  and and_7 (and_7_out, Boton4, shift_register_9_q11[2]);
  or or_2 (salidaPuntaje, and_4_out, and_5_out, and_6_out, and_7_out);
endmodule

module ConectorMatriz (
  input  PINConfig,
  input  [11:0] COL3GRABAR,
  input  [11:0] COL4GRABAR,
  input  [11:0] COL1GRABAR,
  input  [11:0] COL2GRABAR,
  input  [11:0] in_6,
  input  [11:0] in_7,
  input  [11:0] in_8,
  input  [11:0] in_9,
  output [11:0] out_10,
  output [11:0] out_11,
  output [11:0] out_12,
  output [11:0] out_13
);

  Multiplexer #(.width(12)) multiplexer_1 (.in0(COL1GRABAR), .in1(in_8), .out(out_12), .sel(PINConfig));
  Multiplexer #(.width(12)) multiplexer_2 (.in0(COL2GRABAR), .in1(in_9), .out(out_13), .sel(PINConfig));
  Multiplexer #(.width(12)) multiplexer_3 (.in0(COL3GRABAR), .in1(in_6), .out(out_10), .sel(PINConfig));
  Multiplexer #(.width(12)) multiplexer_4 (.in0(COL4GRABAR), .in1(in_7), .out(out_11), .sel(PINConfig));
endmodule
